// Logisim project CPU.circ as structural Verilog: 9 circuits, main circuit main
module main (
  input  reset,
  output [31:0] out_2,
  output [31:0] out_3,
  output out_4,
  output [4:0] out_5,
  output [31:0] out_6,
  output out_7,
  output [31:0] out_8,
  output [31:0] out_9
);

  wire clock_1_out, comparator_1_eq, EXTOp, isZero;
  wire [1:0] ALUBSel, DMSel, GRFA3Sel, GRFWDSel, NPCOp;
  wire [2:0] ALUOp;
  wire [4:0] undriven;
  wire [31:0] adder_1_out, dm_1_rd, ext_1_ext, multiplexer_4_out, npc_1_npc, PC4, PC_q, ra;

  NPC npc_1 (.PC(out_3), .IMM(out_2[25:0]), .PC4(PC4), .NPC(npc_1_npc), .NPCOp(NPCOp), .isZero(isZero), .ra(ra));
  Adder #(.width(32)) adder_1 (.a(PC_q), .b(32'h3000), .out(adder_1_out));  // open: cin, cout
  Clock clock_1 (.out(clock_1_out));
  Comparator #(.width(32)) comparator_1 (.a({32{1'b0}}), .b(PC_q), .eq(comparator_1_eq));  // open: gt, lt
  Register #(.width(32)) PC (.D(npc_1_npc), .Q(PC_q), .clk(clock_1_out), .clr(reset));  // open: en
  // Probe on out_2
  Multiplexer #(.width(32), .enable("false")) multiplexer_1 (
    .in0(PC_q), .in1(adder_1_out), .out(out_3), .sel(comparator_1_eq));
  IM im_1 (.A(out_3), .D(out_2));
  CTRL ctrl_1 (
    .Op0(out_2[26]), .Op1(out_2[27]), .Op2(out_2[28]), .Op3(out_2[29]), .Op4(out_2[30]), .Op5(out_2[31]),
    .Func0(out_2[0]), .Func1(out_2[1]), .Func2(out_2[2]), .Func3(out_2[3]), .Func4(out_2[4]),
    .Func5(out_2[5]), .NPCOp(NPCOp), .GRFWr(out_4), .EXTOp(EXTOp), .ALUOp(ALUOp), .DMWr(out_7),
    .GRFA3Sel(GRFA3Sel), .GRFWDSel(GRFWDSel), .ALUBSel(ALUBSel), .DMSel(DMSel));
  EXT ext_1 (.IMM16(out_2[15:0]), .Ext(ext_1_ext), .in_1(EXTOp));
  Multiplexer #(.select(2), .width(5), .enable("false")) multiplexer_2 (
    .in0(out_2[20:16]), .in1(out_2[15:11]), .in2({5{1'b1}}), .in3(undriven), .out(out_5), .sel(GRFA3Sel));
  Multiplexer #(.select(2), .width(32), .enable("false")) multiplexer_3 (
    .in0(out_8), .in1(dm_1_rd), .in2(PC4), .out(out_6), .sel(GRFWDSel));  // open: in3
  GRF grf_1 (
    .A1(out_2[25:21]), .A2(out_2[20:16]), .A3(out_5), .WD(out_6), .out_8(ra), .out_9(out_9),
    .in_7(clock_1_out), .RST(reset), .WE(out_4));
  Multiplexer #(.select(2), .width(32), .enable("false")) multiplexer_4 (
    .in0(out_9), .in1(ext_1_ext), .out(multiplexer_4_out), .sel(ALUBSel));  // open: in2, in3
  ALU alu_1 (.A(ra), .B(multiplexer_4_out), .C(out_8), .in_3(ALUOp), .isZero(isZero));
  DM dm_1 (.A(out_8), .WD(out_9), .RD(dm_1_rd), .DMWr(out_7), .CLK(clock_1_out), .RST(reset), .DMSel(DMSel));

  // Other names for the same wires on the sheet: DMWr = out_7; GRFWr = out_4; Instr[31:0] = out_2;
  //   MemAddr[31:0] = out_8; MemData[31:0] = out_9; pc[31:0] = out_3; RegAddr[4:0] = out_5; RegData[31:0] = out_6

  // Notes on the sheet:
  //   opcode
endmodule

module NPC (
  input  [31:0] PC,
  input  [25:0] IMM,
  input  [1:0] NPCOp,
  input  isZero,
  input  [31:0] ra,
  output [31:0] PC4,
  output [31:0] NPC
);

  wire [31:0] adder_2_out, bit_extender_1_out, multiplexer_1_out;

  Adder #(.width(32)) adder_1 (.a(PC), .b(32'h4), .out(PC4));  // open: cin, cout
  assign bit_extender_1_out = {{14{IMM[15]}}, {IMM[15:0], 2'b00}};  // Bit_Extender bit_extender_1
  Adder #(.width(32)) adder_2 (.a(PC4), .b(bit_extender_1_out), .out(adder_2_out));  // open: cin, cout
  Multiplexer #(.width(32), .enable("false")) multiplexer_1 (
    .in0(PC4), .in1(adder_2_out), .out(multiplexer_1_out), .sel(isZero));
  Multiplexer #(.select(2), .width(32), .enable("false")) multiplexer_2 (
    .in0(PC4), .in1(multiplexer_1_out), .in2({PC[31:28], IMM, 2'b00}), .in3(ra), .out(NPC), .sel(NPCOp));

  // Other names for the same wires on the sheet: IMM26[25:0] = IMM
endmodule

module GRF (
  input  [4:0] A1,
  input  WE,
  input  [4:0] A2,
  input  [4:0] A3,
  input  [31:0] WD,
  input  RST,
  input  in_7,
  output [31:0] out_8,
  output [31:0] out_9
);

  wire multiplexer_1_out, we_0, we_1, we_2, we_3, we_4, we_5, we_6, we_7, we_8, we_9, we_10, we_11, we_12,
       we_13, we_14, we_15, we_16, we_17, we_18, we_19, we_20, we_21, we_22, we_23, we_24, we_25, we_26,
       we_27, we_28, we_29, we_30, we_31;
  wire [31:0] rd_1, rd_2, rd_3, rd_4, rd_5, rd_6, rd_7, rd_8, rd_9, rd_10, rd_11, rd_12, rd_13, rd_14, rd_15,
       rd_16, rd_17, rd_18, rd_19, rd_20, rd_21, rd_22, rd_23, rd_24, rd_25, rd_26, rd_27, rd_28, rd_29,
       rd_30, rd_31, write_0, write_1, write_2, write_3, write_4, write_5, write_6, write_7, write_8,
       write_9, write_10, write_11, write_12, write_13, write_14, write_15, write_16, write_17, write_18,
       write_19, write_20, write_21, write_22, write_23, write_24, write_25, write_26, write_27, write_28,
       write_29, write_30, write_31;

  Register #(.width(32)) _0 (.D(write_0), .en(we_0), .clk(in_7), .clr(RST));  // open: Q
  Register #(.width(32)) _1 (.D(write_1), .en(we_1), .Q(rd_1), .clk(in_7), .clr(RST));
  Register #(.width(32)) _2 (.D(write_2), .en(we_2), .Q(rd_2), .clk(in_7), .clr(RST));
  Register #(.width(32)) _3 (.D(write_3), .en(we_3), .Q(rd_3), .clk(in_7), .clr(RST));
  Register #(.width(32)) _4 (.D(write_4), .en(we_4), .Q(rd_4), .clk(in_7), .clr(RST));
  Register #(.width(32)) _5 (.D(write_5), .en(we_5), .Q(rd_5), .clk(in_7), .clr(RST));
  Register #(.width(32)) _6 (.D(write_6), .en(we_6), .Q(rd_6), .clk(in_7), .clr(RST));
  Register #(.width(32)) _7 (.D(write_7), .en(we_7), .Q(rd_7), .clk(in_7), .clr(RST));
  Register #(.width(32)) _8 (.D(write_8), .en(we_8), .Q(rd_8), .clk(in_7), .clr(RST));
  Register #(.width(32)) _9 (.D(write_9), .en(we_9), .Q(rd_9), .clk(in_7), .clr(RST));
  Register #(.width(32)) _10 (.D(write_10), .en(we_10), .Q(rd_10), .clk(in_7), .clr(RST));
  Register #(.width(32)) _11 (.D(write_11), .en(we_11), .Q(rd_11), .clk(in_7), .clr(RST));
  Register #(.width(32)) _12 (.D(write_12), .en(we_12), .Q(rd_12), .clk(in_7), .clr(RST));
  Register #(.width(32)) _13 (.D(write_13), .en(we_13), .Q(rd_13), .clk(in_7), .clr(RST));
  Register #(.width(32)) _14 (.D(write_14), .en(we_14), .Q(rd_14), .clk(in_7), .clr(RST));
  Register #(.width(32)) _15 (.D(write_15), .en(we_15), .Q(rd_15), .clk(in_7), .clr(RST));
  Register #(.width(32)) _16 (.D(write_16), .en(we_16), .Q(rd_16), .clk(in_7), .clr(RST));
  Register #(.width(32)) _17 (.D(write_17), .en(we_17), .Q(rd_17), .clk(in_7), .clr(RST));
  Register #(.width(32)) _18 (.D(write_18), .en(we_18), .Q(rd_18), .clk(in_7), .clr(RST));
  Register #(.width(32)) _19 (.D(write_19), .en(we_19), .Q(rd_19), .clk(in_7), .clr(RST));
  Register #(.width(32)) _20 (.D(write_20), .en(we_20), .Q(rd_20), .clk(in_7), .clr(RST));
  Register #(.width(32)) _21 (.D(write_21), .en(we_21), .Q(rd_21), .clk(in_7));  // open: clr
  Register #(.width(32)) _22 (.D(write_22), .en(we_22), .Q(rd_22), .clk(in_7), .clr(RST));
  Register #(.width(32)) _23 (.D(write_23), .en(we_23), .Q(rd_23), .clk(in_7), .clr(RST));
  Register #(.width(32)) _24 (.D(write_24), .en(we_24), .Q(rd_24), .clk(in_7), .clr(RST));
  Register #(.width(32)) _25 (.D(write_25), .en(we_25), .Q(rd_25), .clk(in_7), .clr(RST));
  Register #(.width(32)) _26 (.D(write_26), .en(we_26), .Q(rd_26), .clk(in_7), .clr(RST));
  Register #(.width(32)) _27 (.D(write_27), .en(we_27), .Q(rd_27), .clk(in_7), .clr(RST));
  Register #(.width(32)) _28 (.D(write_28), .en(we_28), .Q(rd_28), .clk(in_7), .clr(RST));
  Register #(.width(32)) _29 (.D(write_29), .en(we_29), .Q(rd_29), .clk(in_7), .clr(RST));
  Register #(.width(32)) _30 (.D(write_30), .en(we_30), .Q(rd_30), .clk(in_7), .clr(RST));
  Register #(.width(32)) _31 (.D(write_31), .en(we_31), .Q(rd_31), .clk(in_7), .clr(RST));
  Multiplexer multiplexer_1 (.in0(1'b0), .in1(1'b1), .out(multiplexer_1_out), .sel(WE));  // open: en
  Demultiplexer #(.select(5), .enable("false")) demultiplexer_1 (
    .out0(we_0), .out1(we_1), .out2(we_2), .out3(we_3), .out4(we_4), .out5(we_5), .out6(we_6), .out7(we_7),
    .out8(we_8), .out9(we_9), .out10(we_10), .out11(we_11), .out12(we_12), .out13(we_13), .out14(we_14),
    .out15(we_15), .out16(we_16), .out17(we_17), .out18(we_18), .out19(we_19), .out20(we_20), .out21(we_21),
    .out22(we_22), .out23(we_23), .out24(we_24), .out25(we_25), .out26(we_26), .out27(we_27), .out28(we_28),
    .out29(we_29), .out30(we_30), .out31(we_31), .in(multiplexer_1_out), .sel(A3));
  Multiplexer #(.select(5), .width(32), .enable("false")) multiplexer_2 (
    .in0({32{1'b0}}), .in1(rd_1), .in2(rd_2), .in3(rd_3), .in4(rd_4), .in5(rd_5), .in6(rd_6), .in7(rd_7),
    .in8(rd_8), .in9(rd_9), .in10(rd_10), .in11(rd_11), .in12(rd_12), .in13(rd_13), .in14(rd_14),
    .in15(rd_15), .in16(rd_16), .in17(rd_17), .in18(rd_18), .in19(rd_19), .in20(rd_20), .in21(rd_21),
    .in22(rd_22), .in23(rd_23), .in24(rd_24), .in25(rd_25), .in26(rd_26), .in27(rd_27), .in28(rd_28),
    .in29(rd_29), .in30(rd_30), .in31(rd_31), .out(out_8), .sel(A1));
  Demultiplexer #(.select(5), .width(32), .enable("false")) demultiplexer_2 (
    .out0(write_0), .out1(write_1), .out2(write_2), .out3(write_3), .out4(write_4), .out5(write_5),
    .out6(write_6), .out7(write_7), .out8(write_8), .out9(write_9), .out10(write_10), .out11(write_11),
    .out12(write_12), .out13(write_13), .out14(write_14), .out15(write_15), .out16(write_16),
    .out17(write_17), .out18(write_18), .out19(write_19), .out20(write_20), .out21(write_21),
    .out22(write_22), .out23(write_23), .out24(write_24), .out25(write_25), .out26(write_26),
    .out27(write_27), .out28(write_28), .out29(write_29), .out30(write_30), .out31(write_31), .in(WD),
    .sel(A3));
  Multiplexer #(.select(5), .width(32), .enable("false")) multiplexer_3 (
    .in0({32{1'b0}}), .in1(rd_1), .in2(rd_2), .in3(rd_3), .in4(rd_4), .in5(rd_5), .in6(rd_6), .in7(rd_7),
    .in8(rd_8), .in9(rd_9), .in10(rd_10), .in11(rd_11), .in12(rd_12), .in13(rd_13), .in14(rd_14),
    .in15(rd_15), .in16(rd_16), .in17(rd_17), .in18(rd_18), .in19(rd_19), .in20(rd_20), .in21(rd_21),
    .in22(rd_22), .in23(rd_23), .in24(rd_24), .in25(rd_25), .in26(rd_26), .in27(rd_27), .in28(rd_28),
    .in29(rd_29), .in30(rd_30), .in31(rd_31), .out(out_9), .sel(A2));

  // Other names for the same wires on the sheet: clk = in_7; en = WE; input[31:0] = WD; RD1[31:0] = out_8;
  //   RD2[31:0] = out_9
endmodule

module IM (
  input  [31:0] A,
  output [31:0] D
);

  wire [11:0] bit_extender_1_out;
  wire [31:0] shifter_1_out, subtractor_1_out;

  Subtractor #(.width(32)) subtractor_1 (.a(A), .b(32'h3000), .out(subtractor_1_out));  // open: bin, bout
  // Probe on shifter_1_out
  // Probe on subtractor_1_out
  Shifter #(.width(32), .shift("lr")) shifter_1 (.in(subtractor_1_out), .\dist (5'b00010), .out(shifter_1_out));
  Bit_Extender #(.in_width(32), .out_width(12)) bit_extender_1 (.in(shifter_1_out), .out(bit_extender_1_out));
  ROM #(.addrWidth(12), .dataWidth(32)) rom_1 (.addr(bit_extender_1_out), .data(D));  // open: sel

  // Notes on the sheet:
  //   contents of rom_1 (hex, n*v repeats v):
  //   35080072 35290202
endmodule

module ALU (
  input  [31:0] A,
  input  [31:0] B,
  input  [2:0] in_3,
  output isZero,
  output [31:0] C
);

  wire [31:0] adder_1_out, adder_2_out, not_1_out, or_1_out;

  assign not_1_out = ~B;  // NOT_Gate not_1, 32 bits wide
  Comparator #(.width(32)) comparator_1 (.a(A), .b(B), .eq(isZero));  // open: gt, lt
  Adder #(.width(32)) adder_1 (.a(A), .b(B), .out(adder_1_out));  // open: cin, cout
  assign or_1_out = A | B;  // OR_Gate or_1, 32 bits wide
  Adder #(.width(32)) adder_2 (.a(A), .b(not_1_out), .out(adder_2_out), .cin(1'b1));  // open: cout
  Multiplexer #(.select(3), .width(32), .enable("false")) multiplexer_1 (
    .in0(adder_1_out), .in1(or_1_out), .in2(adder_2_out), .in3({B[15:0], A[15:0]}), .out(C), .sel(in_3));  // open: in4, in5, in6, in7

  // Notes on the sheet:
  //   000：ADD 001:ORI 010:SUB 011:LUI 100:
endmodule

module EXT (
  input  in_1,
  input  [15:0] IMM16,
  output [31:0] Ext
);

  wire [31:0] bit_extender_1_out, bit_extender_2_out;

  assign bit_extender_1_out = {{16{1'b0}}, IMM16};  // Bit_Extender bit_extender_1
  assign bit_extender_2_out = {{16{IMM16[15]}}, IMM16};  // Bit_Extender bit_extender_2
  Multiplexer #(.width(32)) multiplexer_1 (
    .in0(bit_extender_1_out), .in1(bit_extender_2_out), .out(Ext), .sel(in_1));  // open: en
endmodule

module DM (
  input  [1:0] DMSel,
  input  [31:0] A,
  input  DMWr,
  input  CLK,
  input  RST,
  input  [31:0] WD,
  output [31:0] RD
);

  wire decoder_1_out0, decoder_1_out1, decoder_1_out2, decoder_1_out3;
  wire [7:0] _0_7, _8_15, _16_23, _24_31, multiplexer_1_out, multiplexer_2_out, multiplexer_3_out,
       multiplexer_4_out, multiplexer_6_out;
  wire [31:0] bit_extender_1_out, multiplexer_5_out;

  Decoder #(.select(2), .enable("false")) decoder_1 (
    .out0(decoder_1_out0), .out1(decoder_1_out1), .out2(decoder_1_out2), .out3(decoder_1_out3), .sel(A[1:0]));
  Multiplexer #(.width(8), .enable("false")) multiplexer_1 (
    .in0(_0_7), .in1(WD[7:0]), .out(multiplexer_1_out), .sel(decoder_1_out0));
  Multiplexer #(.width(8), .enable("false")) multiplexer_2 (
    .in0(_8_15), .in1(WD[7:0]), .out(multiplexer_2_out), .sel(decoder_1_out1));
  Multiplexer #(.width(8), .enable("false")) multiplexer_3 (
    .in0(_16_23), .in1(WD[7:0]), .out(multiplexer_3_out), .sel(decoder_1_out2));
  Multiplexer #(.width(8), .enable("false")) multiplexer_4 (
    .in0(_24_31), .in1(WD[7:0]), .out(multiplexer_4_out), .sel(decoder_1_out3));
  Multiplexer #(.select(2), .width(32), .enable("false")) multiplexer_5 (
    .in0(WD), .in1({multiplexer_4_out, multiplexer_3_out, multiplexer_2_out, multiplexer_1_out}),
    .out(multiplexer_5_out), .sel(DMSel));  // open: in2, in3
  RAM #(.addrWidth(5), .dataWidth(32), .bus("separate")) ram_1 (
    .addr(A[6:2]), .din(multiplexer_5_out), .data({_24_31, _16_23, _8_15, _0_7}), .str(DMWr), .clk(CLK),
    .clr(RST));  // open: sel, ld
  Multiplexer #(.select(2), .width(8), .enable("false")) multiplexer_6 (
    .in0(_0_7), .in1(_8_15), .in2(_16_23), .in3(_24_31), .out(multiplexer_6_out), .sel(A[1:0]));
  assign bit_extender_1_out = {{24{multiplexer_6_out[7]}}, multiplexer_6_out};  // Bit_Extender bit_extender_1
  Multiplexer #(.select(2), .width(32), .enable("false")) multiplexer_7 (
    .in0({_24_31, _16_23, _8_15, _0_7}), .in1(bit_extender_1_out), .out(RD), .sel(DMSel));  // open: in2, in3
endmodule

module AND (
  input  Op0,
  input  Op1,
  input  Op2,
  input  Op3,
  input  Op4,
  input  Op5,
  output SPECIAL,
  output ORI,
  output LUI,
  output LW,
  output SW,
  output BEQ,
  output JAL,
  output LB,
  output SB
);

  wire not_1_out, not_2_out, not_3_out, not_4_out, not_5_out, not_6_out;

  not not_1 (not_1_out, Op0);
  not not_2 (not_2_out, Op1);
  not not_3 (not_3_out, Op2);
  not not_4 (not_4_out, Op3);
  not not_5 (not_5_out, Op4);
  not not_6 (not_6_out, Op5);
  and and_1 (SPECIAL, not_6_out, not_5_out, not_4_out, not_3_out, not_2_out, not_1_out);
  and and_2 (ORI, not_6_out, not_5_out, Op3, Op2, not_2_out, Op0);
  and and_3 (LUI, not_6_out, not_5_out, Op3, Op2, Op1, Op0);
  and and_4 (LW, Op5, not_5_out, not_4_out, not_3_out, Op1, Op0);
  and and_5 (SW, Op5, not_5_out, Op3, not_3_out, Op1, Op0);
  and and_6 (BEQ, not_6_out, not_5_out, not_4_out, Op2, not_2_out, not_1_out);
  and and_7 (JAL, not_6_out, not_5_out, not_4_out, not_3_out, Op1, Op0);
  and and_8 (LB, Op5, not_5_out, not_4_out, not_3_out, not_2_out, not_1_out);
  and and_9 (SB, Op5, not_5_out, Op3, not_3_out, not_2_out, not_1_out);
endmodule

module CTRL (
  input  Op0,
  input  Op1,
  input  Op2,
  input  Op3,
  input  Op4,
  input  Op5,
  input  Func0,
  input  Func1,
  input  Func2,
  input  Func3,
  input  Func4,
  input  Func5,
  output GRFWr,
  output EXTOp,
  output DMWr,
  output [2:0] ALUOp,
  output [1:0] GRFA3Sel,
  output [1:0] GRFWDSel,
  output [1:0] ALUBSel,
  output [1:0] DMSel,
  output [1:0] NPCOp
);

  wire Add_u, Beq, Jal, JR, Lb, Lui, Lw, not_1_out, not_2_out, not_3_out, not_4_out, not_5_out, not_6_out,
       Ori, Sb, special, Sub_u, Sw;

  AND and_1 (
    .Op0(Op0), .Op1(Op1), .Op2(Op2), .Op3(Op3), .Op4(Op4), .Op5(Op5), .SPECIAL(special), .ORI(Ori),
    .LUI(Lui), .LW(Lw), .SW(Sw), .BEQ(Beq), .JAL(Jal), .LB(Lb), .SB(Sb));
  not not_1 (not_1_out, Func0);
  not not_2 (not_2_out, Func1);
  not not_3 (not_3_out, Func2);
  not not_4 (not_4_out, Func3);
  not not_5 (not_5_out, Func4);
  not not_6 (not_6_out, Func5);
  and and_2 (Add_u, Func5, not_5_out, not_4_out, special, not_3_out, not_2_out, not_1_out);
  or or_1 (NPCOp[1], 1'b0, Jal, JR);
  and and_3 (Sub_u, Func5, not_5_out, not_4_out, special, not_3_out, Func1, not_1_out);
  or or_2 (NPCOp[0], Beq, JR);
  and and_4 (JR, not_6_out, not_5_out, Func3, special, not_3_out, not_2_out, not_1_out);
  or or_3 (GRFWr, Lb, Jal, Ori, Lui, Lw, Sub_u, Add_u);
  or or_4 (EXTOp, Sb, Lb, Lui, Lw, Sw);
  buf or_5 (ALUOp[2], 1'b0);  // OR_Gate
  or or_6 (ALUOp[1], Sub_u, Lui);
  or or_7 (ALUOp[0], Lui, Ori);
  or or_8 (DMWr, Sb, Sw);
  or or_9 (GRFA3Sel[1], 1'b0, Jal);
  or or_10 (GRFA3Sel[0], Sub_u, Add_u);
  or or_11 (GRFWDSel[1], 1'b0, Jal);
  or or_12 (GRFWDSel[0], Lb, Lw);
  buf or_13 (ALUBSel[1], 1'b0);  // OR_Gate
  or or_14 (ALUBSel[0], Sb, Lb, Ori, Lui, Lw, Sw);
  buf or_15 (DMSel[1], 1'b0);  // OR_Gate
  or or_16 (DMSel[0], Sb, Lb);
endmodule
